# Fritzing sketch brewflowmeter-breadborad (saved by Fritzing 0.9.1b)

parts:
  Arduino = Arduino Uno (Rev3)
  5v/12v_Relay = Relay [part_number=FRS1B-S package=THT]
  LCD = LCD screen
  R1 = Trimmer Potentiometer [maximum_resistance=10kΩ package=THT]
  Rotary_Encoder = Rotary Encoder [package=THT]
  Solenoid_Valve = Solenoid

nets:
  N1: Arduino.D8, LCD.DB6
  N2: Arduino.D9_PWM, LCD.DB5
  N3: Arduino.D10_PWM/SS, LCD.DB4
  N4: Arduino.D11_PWM/MOSI, LCD.E
  N5: Arduino.D12/MISO, LCD.RS
  GND: Arduino.GND, 5v/12v_Relay.COIL2, LCD.VSS, LCD.R/W, R1.leg1, Rotary_Encoder.EncoderPinA
  N6: Arduino.D3_PWM, Rotary_Encoder.EncoderPinC
  N7: Arduino.D4, 5v/12v_Relay.COIL1
  N8: Arduino.D7, LCD.DB7
  5V: Arduino.5V, LCD.VDD, R1.leg2, Rotary_Encoder.EncoderPinB
  N9: 5v/12v_Relay.C1, 5v/12v_Relay.C2, Solenoid_Valve.pin2
  N10: LCD.V0, R1.wiper
